# Fritzing sketch task (saved by Fritzing 0.8.7b)
breadboards: 1

parts:
  R1 = Resistor [tolerance=±5% resistance=220 package=THT]
  R2 = Rotary Potentiometer (Small) [maximum_resistance=100kΩ package=THT]
  Часть1 = Arduino Uno (Rev3)
  R3 = Resistor [tolerance=±5% resistance=220 package=THT]
  C1 = Tantalum Capacitor [capacitance=1μF package="100 mil [THT, tantalum]"]
  C2 = Tantalum Capacitor [capacitance=1μF package="100 mil [THT, tantalum]"]

nets:
  N1: R1.Pin_0, Часть1.D11_PWM/MOSI
  N2: R1.Pin_1, C2.+
  N3: R2.leg1, Часть1.5V
  N4: R2.leg2, Часть1.GND, C1.-, C2.-
  N5: Часть1.D9_PWM, R3.Pin_1
  N6: R3.Pin_0, C1.+
